// Digital circuit 4bit-computer.dig as structural Verilog
module _4bit_computer (
  input  in_1,
  input  in_2,
  input  in_3,
  input  in_4,
  input  A_M,
  input  Write,
  input  Read_EE,
  input  Read_EB,
  input  Read_rC,
  input  Reset,
  input  Clock,
  input  Read_rA,
  input  Read_rB,
  input  Write_to_RAM,
  input  Write_to_Bus,
  input  APU_to_Bus,
  input  Flags,
  input  Minus,
  input  Read_Addresses
);

  wire address_register_1__1, address_register_1__2, address_register_1__4, address_register_1__8,
       instructions_1_p5, instructions_1_p6, ram_storage_1_out_1, ram_storage_1_out_2, ram_storage_1_out_4,
       ram_storage_1_out_8, register_1_out_1, register_1_out_2, register_1_out_4, register_1_out_8,
       register_3_out_1, register_3_out_2, register_3_out_4, register_3_out_8,
       registers_and_programmer_1_b_1, registers_and_programmer_1_b_2, registers_and_programmer_1_b_4,
       registers_and_programmer_1_b_8, registers_and_programmer_1_e_1, registers_and_programmer_1_e_2,
       registers_and_programmer_1_e_4, registers_and_programmer_1_e_8;

  RAM_storage ram_storage_1 (
    .Bus(Write_to_Bus), .Save(Write_to_RAM), .B_8(registers_and_programmer_1_b_8),
    .B_4(registers_and_programmer_1_b_4), .B_2(registers_and_programmer_1_b_2),
    .B_1(registers_and_programmer_1_b_1), .E_8(registers_and_programmer_1_e_8),
    .E_4(registers_and_programmer_1_e_4), .E_2(registers_and_programmer_1_e_2),
    .E_1(registers_and_programmer_1_e_1), .AR_1(address_register_1__1), .AR_2(address_register_1__2),
    .AR_4(address_register_1__4), .AR_8(address_register_1__8), .Bus_1(in_4), .Bus_2(in_3), .Bus_4(in_2),
    .Bus_8(in_1), .Out_1(ram_storage_1_out_1), .Out_2(ram_storage_1_out_2), .Out_4(ram_storage_1_out_4),
    .Out_8(ram_storage_1_out_8));
  Address_register address_register_1 (
    .Reset(Reset), .Read(Read_Addresses), .Clock(Clock), .Bus_8(in_1), .Bus_4(in_2), .Bus_2(in_3),
    .Bus_1(in_4), ._1(address_register_1__1), ._2(address_register_1__2), ._4(address_register_1__4),
    ._8(address_register_1__8));
  Registers_and_Programmer registers_and_programmer_1 (
    .Reset(Reset), .Clock(Clock), .Write(Write), .Read_E(Read_EB), .Read_B(Read_EE),
    .D_8(address_register_1__8), .D_4(address_register_1__4), .D_2(address_register_1__2),
    .D_1(address_register_1__1), .Bus_8(in_1), .Bus_4(in_2), .Bus_2(in_3), .Bus_1(in_4),
    .E_8(registers_and_programmer_1_e_8), .E_4(registers_and_programmer_1_e_4),
    .E_2(registers_and_programmer_1_e_2), .E_1(registers_and_programmer_1_e_1),
    .B_8(registers_and_programmer_1_b_8), .B_4(registers_and_programmer_1_b_4),
    .B_2(registers_and_programmer_1_b_2), .B_1(registers_and_programmer_1_b_1));
  // Instructions instructions_1: pin names not known; wires that end beside it: ram_storage_1_out_8, ram_storage_1_out_4, ram_storage_1_out_2, ram_storage_1_out_1, instructions_1_p5, instructions_1_p6, A_M
  APU apu_1 (
    .rA_8(register_1_out_8), .rA_4(register_1_out_4), .rA_2(register_1_out_2), .rA_1(register_1_out_1),
    .Reset(Reset), .Bus(APU_to_Bus), .Flags(Flags), .Clock(Clock), .Minus(Minus), .rB_8(register_3_out_8),
    .rB_4(register_3_out_4), .rB_2(register_3_out_2), .rB_1(register_3_out_1),
    .Flag_OverFlow(instructions_1_p6), .Flag_Negative(instructions_1_p5), .Bus_8(in_1), .Bus_4(in_2),
    .Bus_2(in_3), .Bus_1(in_4));
  register register_1 (
    ._8(in_1), ._4(in_2), ._2(in_3), ._1(in_4), .Reset(Reset), .Read(Read_rA), .Clock(Clock),
    .Out_8(register_1_out_8), .Out_4(register_1_out_4), .Out_2(register_1_out_2), .Out_1(register_1_out_1));
  register register_2 (
    ._8(in_1), ._4(in_2), ._2(in_3), ._1(in_4), .Reset(Reset), .Read(Read_rC), .Clock(Clock));  // open: Out_8, Out_4, Out_2, Out_1
  register register_3 (
    ._8(in_1), ._4(in_2), ._2(in_3), ._1(in_4), .Reset(Reset), .Read(Read_rB), .Clock(Clock),
    .Out_8(register_3_out_8), .Out_4(register_3_out_4), .Out_2(register_3_out_2), .Out_1(register_3_out_1));
endmodule
